# Fritzing sketch ArdEos Actual (saved by Fritzing 0.9.2b)
circuit board: 11.2844cm x 6.12539cm
breadboards: 1

parts:
  C4 = Tantalum Capacitor [capacitance=1μF package="100 mil [THT, tantalum]"]
  C5 = Tantalum Capacitor [capacitance=1μF package="100 mil [THT, tantalum]"]
  C1 = Tantalum Capacitor [capacitance=1μF package="100 mil [THT, tantalum]"]
  C2 = Tantalum Capacitor [capacitance=1μF package="100 mil [THT, tantalum]"]
  C3 = Tantalum Capacitor [capacitance=1μF package="100 mil [THT, tantalum]"]
  Adafruit_HUZZAH_ESP8266_Breakout2 = Adafruit HUZZAH ESP8266 Breakout [part_number=2471]
  U4 = Voltage Regulator - 5V [package="TO220 [THT]"]
  U5 = RS232 Transceiver [package=dil16]
  C6 = Ceramic Capacitor [capacitance=100nF package="100 mil [THT, multilayer]"]
  C7 = Ceramic Capacitor [capacitance=100nF package="100 mil [THT, multilayer]"]
  J1 = female pin header, 2 pins [form="♀ (female)"]
  J2 = female pin header, 2 pins [form="♀ (female)"]
  J3 = female pin header, 2 pins [form="♀ (female)"]

nets:
  N1: C4.-, U5.V-
  N2: C4.+, C3.-
  GND: C5.-, U4.GND, U5.GND, C6.0, C7.0, J1.pin2, J3.pin2
  N3: C5.+, Adafruit_HUZZAH_ESP8266_Breakout2.3V, U5.VCC
  N4: C1.-, U5.C1-
  N5: C1.+, U5.C1+
  N6: C2.-, U5.C2-
  N7: C2.+, U5.C2+
  N8: C3.+, U5.V+
  N9: Adafruit_HUZZAH_ESP8266_Breakout2.VBat, U4.output_voltage, C6.1
  N10: Adafruit_HUZZAH_ESP8266_Breakout2.TX, U5.T1IN
  N11: Adafruit_HUZZAH_ESP8266_Breakout2.RX, U5.R1OUT
  N12: U4.input_voltage, C7.1, J1.pin1, J3.pin1
  N13: U5.R1IN, J2.pin2
  N14: U5.T1OUT, J2.pin1
